# Fritzing sketch tarefa1 (saved by Fritzing 0.9.3b)
breadboards: 1

parts:
  Componente1 = Arduino Nano (Rev3.0)
  U1 = POT [package=pot_mammoth]
  R1 = Resistor [tolerance=±5% resistance=330 package=THT]
  LED1 = smd LED [color="Red (633nm)" package="1206 [SMD]"]

nets:
  N1: Componente1.D3, R1.Pin_0
  N2: Componente1.GND, U1.S, LED1.cathode
  N3: Componente1.5V, U1.E
  N4: Componente1.A0, U1.A
  N5: R1.Pin_1, LED1.anode
