# Fritzing sketch tarefa3 (saved by Fritzing 0.9.3b)
breadboards: 1

parts:
  Componente1 = Arduino Nano (Rev3.0)
  S1 = Pushbutton [package="[THT]"]
  R1 = Resistor [tolerance=±5% resistance=220 package=THT]
  LED1 = smd LED [color="Red (660nm)" package="1206 [SMD]"]

nets:
  N1: Componente1.D2, R1.Pin_1
  N2: Componente1.D3, S1.Pin_1, S1.Pin_2
  N3: Componente1.GND, S1.Pin_3, S1.Pin_4, LED1.cathode
  N4: R1.Pin_0, LED1.anode
