# Fritzing sketch tarefa1 (saved by Fritzing 0.9.3b)
breadboards: 1

parts:
  T1 = LM35 Temperature Sensor [package="TO92 [THT]"]
  Componente1 = Arduino Nano (Rev3.0)
  Grove1 = Grove OLED 128x96

nets:
  5V: T1.+Vs, Componente1.5V, Grove1.VCC
  N1: T1.Vout, Componente1.A0
  GND: T1.GND, Componente1.GND, Grove1.GND
  N2: Componente1.A5, Grove1.SCL
  N3: Componente1.A4, Grove1.SDA
