# Fritzing sketch tarefa2 (saved by Fritzing 0.9.3b)
breadboards: 1

parts:
  Componente1 = Arduino Nano (Rev3.0)
  LED1 = LED - 5mm [color="Red (633nm)" package="5 mm [THT]"]
  R1 = Resistor [tolerance=±5% resistance=330 package="2512 [SMD]"]
  S2 = Momentary Switch [package=ksa_sealed_tac_switch]

nets:
  N1: Componente1.D2, S2.1, S2.2
  N2: Componente1.D3, R1.Pin_1
  N3: Componente1.GND, LED1.cathode, S2.3, S2.4
  N4: LED1.anode, R1.Pin_0
