# Fritzing sketch fadingResolution (saved by Fritzing 0.9.3b)
breadboards: 1

parts:
  U1 = POT [package=pot_mammoth]
  R1 = Resistor [tolerance=±5% resistance=330 package=THT]
  LED1 = smd LED [color="Red (633nm)" package="1206 [SMD]"]
  Componente2 = Intel Galileo Gen2

nets:
  N1: U1.S, LED1.cathode, Componente2.GND
  N2: U1.A, Componente2.A0
  N3: U1.E, Componente2.5V
  N4: R1.Pin_0, Componente2.D3_PWM
  N5: R1.Pin_1, LED1.anode
