# Fritzing sketch tarefa2 (saved by Fritzing 0.9.3b)
breadboards: 1

parts:
  Componente1 = Intel Galileo Gen2
  LED1 = LED - 5mm [color="Red (633nm)" package="5 mm [THT]"]
  R1 = Resistor [tolerance=±5% resistance=330 package="0603 [SMD]"]

nets:
  N1: Componente1.D13/SCK, R1.Pin_1
  N2: Componente1.GND, LED1.cathode
  N3: LED1.anode, R1.Pin_0
