# Fritzing sketch mqSensor (saved by Fritzing 0.9.3b)

parts:
  Componente1 = Arduino Nano (Rev3.0)
  Raspberry_Pi_1 = Raspberry Pi 3 [part_number=RPI-3-V1.2]  # not connected
  U1 = GAS_SENSOR [package=mq-3]

nets:
  N1: Componente1.GND, U1.A1
  N2: Componente1.5V, U1.B1
