# Fritzing sketch bme280 (saved by Fritzing 0.9.3b)

parts:
  Componente1 = Arduino Nano (Rev3.0)
  Componente2 = BME280 Breakout
  Raspberry_Pi_1 = Raspberry Pi 3 [part_number=RPI-3-V1.2]  # not connected

nets:
  GND: Componente1.GND, Componente2.GND
  5V: Componente1.5V, Componente2.3.3V
  N1: Componente1.A5, Componente2.SCK/SCL
  N2: Componente1.A4, Componente2.SDI/SDA
